# Fritzing sketch fritzing_circuit (saved by Fritzing 1.0.5)
breadboards: 1

parts:
  Q1 = Basic FET P-Channel [package="TO220 [THT]"]
  M1 = DC Motor [voltage_(max)=6V voltage_(min)=3V]
  A1 = Raspberry Pi Pico2
  Capacitive_Soil_Moisture_Sensor1 = DFRobot Capacitive Soil Moisture Sensor V1.0 [part_number=SEN0193]
  U1 = WS2812 RGB LED strip
  R1 = Resistor [tolerance=±5% power=0.25W resistance=470 package=THT]

nets:
  N1: Q1.gate, A1.pin_20
  GND: Q1.drain, A1.pin_3, A1.pin_8, A1.pin_13, A1.pin_18, A1.pin_23, A1.pin_28, A1.pin_33, A1.pin_38, A1.pin_42, Capacitive_Soil_Moisture_Sensor1.GND, U1.GND
  N2: Q1.source, M1.pin_1
  N3: M1.pin_2, A1.pin_40, U1.VCC
  N4: A1.pin_2, R1.Pin_1
  N5: A1.pin_31, Capacitive_Soil_Moisture_Sensor1.A
  N6: A1.pin_36, Capacitive_Soil_Moisture_Sensor1.VCC
  N7: U1.DIN, R1.Pin_0

custom parts:
  Raspberry Pi Pico2: Raspberry Pi Pico 2W is our new $7 microcontroller board, built on RP2350: our new high-performance, secure microcontroller with on board WiFi.
  DFRobot Capacitive Soil Moisture Sensor V1.0: DFRobot Capacitive Soil Moisture Sensor V1.0 This product measures soil moisture levels by capacitive sensing, rather than resistive sensing like other types of moisture sensor. It is made of a corrosion resistant material giving it a long service life. Insert it into soil and impress your friends with the real-time soil moisture data! The product includes an on-board voltage regulator which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
  WS2812 RGB LED strip: WS2812 strip
